# Fritzing sketch PiPower (saved by Fritzing 0.9.3b)
circuit board: 8.46667cm x 5.64444cm
stripboards: 1

parts:
  Q1 = Basic FET N-Channel [package="TO220 [THT]"]
  R1 = Resistor [tolerance=±5% resistance=10k package=THT]
  U1 = atmega328 [package=dip]
  F3 = Resettable Fuse PTC [package=ptc]
  JP2 = Header 6 [package=molex-1x6-ra]
  Q2 = TRANSISTOR_NPN [part_number=2N2222 package=to-92-ammo]
  R2 = Resistor [tolerance=±5% resistance=1k package=THT]
  J1 = double row female pin header, 12 pins [form="♀ (female)"]
  J3 = female pin header, 6 pins [form="♀ (female)"]
  C1 = Ceramic Capacitor [capacitance=100nF package="100 mil [THT, multilayer]"]
  C2 = Ceramic Capacitor [capacitance=100nF package="100 mil [THT, multilayer]"]
  C3 = Ceramic Capacitor [capacitance=100nF package="100 mil [THT, multilayer]"]
  F4 = Resettable Fuse PTC [package=ptc]
  JP3 = Header 6 [package=molex-1x6-ra]
  F5 = Resettable Fuse PTC [package=ptc]
  U2 = Voltage Regulator [package=to220-adj]
  R3 = Resistor [tolerance=±5% resistance=240 package=THT]
  R4 = Resistor [tolerance=±5% resistance=390 package=THT]

nets:
  PiControl0: Q1.gate, R1.Pin_0, U1.D12
  N1: Q1.drain, J1.pin10, JP3.2
  GND: Q1.source, R1.Pin_1, U1.GND, JP2.1, Q2.E, J3.pin6, C2.1, C3.0, R4.Pin_1
  N2: U1.RESET, C1.0
  N3: U1.D0_(RX), J3.pin3
  N4: U1.D1_(TX), J3.pin2
  N5: U1.VCC, U1.AVCC, J3.pin4, C2.0, C3.1, U2.OUT
  N6: U1.D13, R2.Pin_0
  N7: U1.A4, J1.pin2, JP3.5
  N8: U1.A5, J1.pin3, JP3.6
  N9: F3.1, JP2.5
  PiPower0: F3.2, J1.pin11, J1.pin12, JP3.1
  N10: JP2.3, F4.1, F5.1
  N11: Q2.B, R2.Pin_1
  N12: Q2.C, JP3.4
  N13: J3.pin1, C1.1
  N14: F4.2, U2.IN, R3.Pin_0
  N15: JP3.3, F5.2
  N16: U2.ADJ, R3.Pin_1, R4.Pin_0
